# Fritzing sketch Wiring (saved by Fritzing 0.9.3b)
breadboards: 1

parts:
  U1 = ESP32S-HiLetgo [part_number=ESP32S-HiLetgo]  # not connected
  R1 = Basic Flex Resistor  # not connected
  R2 = Basic Flex Resistor  # not connected
  U2 = Vibration Motor- ROB-08449 [package=vibe-motor-10mm]  # not connected
  U3 = Vibration Motor- ROB-08449 [package=vibe-motor-10mm]  # not connected
  U4 = Vibration Motor- ROB-08449 [package=vibe-motor-10mm]  # not connected
  U5 = Vibration Motor- ROB-08449 [package=vibe-motor-10mm]  # not connected
  J1 = Piezo Speaker  # not connected
  LED2 = smd LED [color="Red (633nm)" package="1206 [SMD]"]
  LED3 = smd LED [color="Red (633nm)" package="1206 [SMD]"]
  S1 = Round Pushbutton
  R3 = Resistor [tolerance=±5% resistance=220 package="2512 [SMD]"]
  R4 = Resistor [tolerance=±5% resistance=220 package="2512 [SMD]"]
  R5 = Resistor [tolerance=±5% resistance=220 package="2512 [SMD]"]
  HLK-PM1 = HLK-PM12 [part_number=HLK-PM12]  # not connected

nets:
  N1: LED2.anode, R5.Pin_1
  N2: LED3.anode, R4.Pin_1
  N3: S1.leg0, R3.Pin_1

custom parts:
  ESP32S-HiLetgo: HiLetgo ESP-WROOM-32 ESP32 ESP-32S Development Board 2.4GHz Dual-Mode WiFi + Bluetooth Dual Cores Microcontroller The ESP32 integrated with Antenna switches, RF Balun, power amplifiers, low-noise amplifiers, filters, and management modules, and the entire solution occupies the least area of PCB. 2.4 GHz Wi-Fi plus Bluetooth dual-mode chip, with TSMC Ultra-low power consumption 40nm technology,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
